# Fritzing sketch IR (saved by Fritzing 0.9.3b)

parts:
  Part1 = Arduino Uno (Rev3)
  IR1 = TSOP312.., 314.. [package=THT]

nets:
  N1: Part1.D2, IR1.GND
  N2: Part1.5V, IR1.Data
  N3: Part1.GND, IR1.Vs

notes:
  TSOP38238 TO ARDUINO UNO
  5V = RED
  GND = BLACK
  BLUE = INFO

// code stored in the sketch: dump.ino
/* dump.ino Example sketch for IRLib2
   Illustrates how to receive an IR signal, decode it and print
   information about it to the serial monitor.
*/
//This includes everything. Not generally recommended.
//It's better to include only the parts of library you really need.
//But for this example it's quick and easy. See "comboDump" example
//for a more efficient way.
#include "IRLibAll.h"

IRrecvPCI myReceiver(2); //create receiver and pass pin number
IRdecode myDecoder;   //create decoder

void setup() {
  Serial.begin(9600);
  delay(2000); while (!Serial); //delay for Leonardo
  myReceiver.enableIRIn(); // Start the receiver
  Serial.println(F("Ready to receive IR signals"));
}

void loop() {
  //Continue looping until you get a complete signal received
  if (myReceiver.getResults()) {
    myDecoder.decode();           //Decode it
    myDecoder.dumpResults(true);  //Now print results. Use false for less detail
    myReceiver.enableIRIn();      //Restart receiver
  }
}
